// Logisim project logic.circ as structural Verilog: 4 circuits, main circuit main
module main (
  input  [2:0] FC
);

  decoder decoder_1 (.A({24{1'b0}}), .SPV(FC[2]));  // open: nIOE, nROME, nETE, nME
endmodule

module decoder (
  input  [23:0] A,
  input  SPV,
  output nIOE,
  output nROME,
  output nETE,
  output nME
);

  wire comparator_1_eq, comparator_2_eq, nIOS, not_2_out, not_4_out, nSAS;

  not not_1 (nME, nSAS);
  not not_2 (not_2_out, A[16]);
  not not_3 (nIOS, comparator_1_eq);
  Comparator #(.width(9), .mode("unsigned")) comparator_1 (
    .a({1'b0, A[15:8]}), .b(9'hff), .eq(comparator_1_eq));  // open: gt, lt
  not not_4 (not_4_out, nIOS);
  or or_1 (nIOE, nIOS, A[16], nSAS);
  or or_2 (nROME, not_4_out, A[16], nSAS);
  or or_3 (nETE, not_2_out, nSAS);
  not not_5 (nSAS, comparator_2_eq);
  Comparator #(.width(9), .mode("unsigned")) comparator_2 (
    .a({1'b0, SPV, A[23:17]}), .b(9'h80), .eq(comparator_2_eq));  // open: gt, lt

  // Other names for the same wires on the sheet: ETS = A[16]

  // Notes on the sheet:
  //   (/enable pin)
  //   (/enable pin)
  //   (IO ports Select)
  //   (Supervisor's Address Space)
  //   (Entries' Table Select)
endmodule

module atu__address_translation_unit (
  input  nETE,
  input  nME
);
endmodule

module int__latcher (
  input  nIE,
  input  nIRQ,
  input  nCLR
);

  wire buffer_1_out, buffer_2_out, IBSY, nor_1_out, nor_2_out, not_1_out, transmission_2_out;
  wire [2:0] IPL_0__2;
  wire [4:4] not_2_out;
  wire [7:0] controlled_buffer_1_out, controlled_buffer_2_out, register_1_q, transmission_out;

  assign controlled_buffer_1_out = nor_1_out ? 8'h4a : 8'bz;  // Controlled_Buffer controlled_buffer_1
  nor nor_1 (nor_1_out, IBSY, nIRQ);
  buf buffer_1 (buffer_1_out, buffer_2_out);
  Pull_Resistor #(.pull(1)) pull_resistor_1 (.node(buffer_1_out));
  buf buffer_2 (buffer_2_out, nIRQ);
  assign transmission_out = controlled_buffer_1_out;  // Buffer transmission, 8 bits wide
  buf transmission_2 (transmission_2_out, buffer_1_out);
  Register register_1 (
    .D({transmission_out[7:5], not_2_out[4], transmission_out[3:0]}), .en(1'b1),
    .Q({register_1_q[7:5], IBSY, register_1_q[3:0]}), .clk(not_2_out[4]), .clr(not_1_out));
  not not_1 (not_1_out, nCLR);
  not not_2 (not_2_out[4], transmission_2_out);
  assign IPL_0__2 = ~register_1_q[7:5];  // NOT_Gate not_3, 3 bits wide
  nor nor_2 (nor_2_out, nIE, nIE);
  assign controlled_buffer_2_out = nor_2_out ? {4'b0100, register_1_q[3:0]} : 8'bz;  // Controlled_Buffer controlled_buffer_2
  // Probe on controlled_buffer_2_out

  // Notes on the sheet:
  //   device
  //   buffer_1 drives only 0 and floats otherwise
  //   RC + schmitt to generate /timeout from IBSY
  //   and between /timeout and edge triggered /IE to generate /CLR
  //   int latcher
endmodule
